# Fritzing sketch Wiring (saved by Fritzing 0.9.5d)
circuit board: 8.46667cm x 5.64444cm
breadboards: 1

parts:
  HC-SR04 = HC-SR04 Ultrasonic Distance Sensor
  LCD_I2C = LCD1602-I2C
  WeMos_D1_Mini1 = WeMos D1 Mini

nets:
  VCC: HC-SR04.VCC, LCD_I2C.VCC, WeMos_D1_Mini1.5V
  N1: HC-SR04.TRIG, WeMos_D1_Mini1.D7
  N2: HC-SR04.ECHO, WeMos_D1_Mini1.D8
  GND: HC-SR04.GND, LCD_I2C.GND, WeMos_D1_Mini1.G
  N3: LCD_I2C.SDA, WeMos_D1_Mini1.D2
  N4: LCD_I2C.SCL, WeMos_D1_Mini1.D1

custom parts:
  LCD1602-I2C: A standard character display, usually with 2x16 characters. Comes in many colors with LCM1602 IIC attached.
